// Logisim project logic-circuit.circ as structural Verilog: 16 circuits, main circuit MainCircuit
module MainCircuit (
  input  Reset
);

  wire Clock_out, controller_1_imm_selector, controller_1_jmp___br_enable, controller_1_jmp___br_selector,
       controller_1_load_enable, controller_1_store_enable, controller_1_write_data_selector,
       controller_1_write_enable;
  wire [1:0] controller_1_alu_type;
  wire [2:0] controller_1_nzp;
  wire [3:0] controller_1_br_address, controller_1_read_address_1, controller_1_read_address_2,
       controller_1_write_address;
  wire [9:0] controller_1_dm_address;
  wire [14:0] controller_1_jmp_address;
  wire [17:0] alu_1_result, branchinstruction_1_address_2, controller_1_imm, datamemory_1_output,
       \instrıctionmemory_1_instruction , jumpinstruction_1_out, multiplexer_1_out, multiplexer_2_out,
       multiplexer_3_out, registerfile_1_read_data_1, registerfile_1_read_data_2;

  Clock Clock (.out(Clock_out));
  \InstrıctionMemory  \instrıctionmemory_1  (
    .JumpAddr(multiplexer_1_out), .Reset(Reset), .Clock(Clock_out),
    .Instruction(\instrıctionmemory_1_instruction ));
  Multiplexer #(.width(18)) multiplexer_1 (
    .in0(jumpinstruction_1_out), .in1(branchinstruction_1_address_2), .out(multiplexer_1_out),
    .sel(controller_1_jmp___br_selector), .en(controller_1_jmp___br_enable));
  JumpInstruction jumpinstruction_1 (.In(controller_1_jmp_address), .Out(jumpinstruction_1_out));
  BranchInstruction branchinstruction_1 (
    .Address(controller_1_br_address), .OP1(registerfile_1_read_data_1), .OP2(registerfile_1_read_data_2),
    .nzp(controller_1_nzp), .Address_2(branchinstruction_1_address_2));
  Controller controller_1 (
    .Instruction(\instrıctionmemory_1_instruction ), .JMP_Address(controller_1_jmp_address),
    .BR_Address(controller_1_br_address), .nzp(controller_1_nzp), .DM_Address(controller_1_dm_address),
    .Imm(controller_1_imm), .Write_Address(controller_1_write_address),
    .Read_Address_1(controller_1_read_address_1), .Read_Address_2(controller_1_read_address_2),
    .Imm_Selector(controller_1_imm_selector), .Write_Enable(controller_1_write_enable),
    .Write_Data_Selector(controller_1_write_data_selector), .Store_Enable(controller_1_store_enable),
    .Load_Enable(controller_1_load_enable), .JMP___BR_Enable(controller_1_jmp___br_enable),
    .JMP___BR_Selector(controller_1_jmp___br_selector), .ALU_Type(controller_1_alu_type));
  Multiplexer #(.width(18), .enable("false")) multiplexer_2 (
    .in0(registerfile_1_read_data_2), .in1(controller_1_imm), .out(multiplexer_2_out),
    .sel(controller_1_imm_selector));
  ALU alu_1 (
    .Reg1(registerfile_1_read_data_1), .Reg2_Or_Imm(multiplexer_2_out), .Type(controller_1_alu_type),
    .Result(alu_1_result));
  Multiplexer #(.width(18), .enable("false")) multiplexer_3 (
    .in0(alu_1_result), .in1(datamemory_1_output), .out(multiplexer_3_out),
    .sel(controller_1_write_data_selector));
  DataMemory datamemory_1 (
    .Address(controller_1_dm_address), .Data(registerfile_1_read_data_1), .Store(controller_1_store_enable),
    .Clock(Clock_out), .Load(controller_1_load_enable), .Clear(Reset), .Output(datamemory_1_output));
  RegisterFile registerfile_1 (
    .Write_Enable(controller_1_write_enable), .Write_Addr(controller_1_write_address),
    .Write_Data(multiplexer_3_out), .Clock(Clock_out), .Clear(Reset),
    .Read_Addr_1(controller_1_read_address_1), .Read_Addr_2(controller_1_read_address_2),
    .Read_Data_1(registerfile_1_read_data_1), .Read_Data_2(registerfile_1_read_data_2));
endmodule

module Controller (
  input  [17:0] Instruction,
  output Imm_Selector,
  output Write_Enable,
  output Write_Data_Selector,
  output Store_Enable,
  output Load_Enable,
  output JMP___BR_Enable,
  output JMP___BR_Selector,
  output [1:0] ALU_Type,
  output [14:0] JMP_Address,
  output [3:0] BR_Address,
  output [2:0] nzp,
  output [9:0] DM_Address,
  output [3:0] Write_Address,
  output [3:0] Read_Address_1,
  output [3:0] Read_Address_2,
  output [17:0] Imm
);

  wire and_4_out, not_1_out, not_2_out, not_3_out, not_4_out;
  wire [3:0] multiplexer_1_out;

  and and_1 (JMP___BR_Enable, Instruction[17], Instruction[16]);
  not not_1 (not_1_out, Instruction[16]);
  and and_2 (Store_Enable, Instruction[17], not_1_out, Instruction[15]);
  _6_18_SignExtender u_6_18_signextender_1 (.In(Instruction[5:0]), .Out(Imm));
  not not_2 (not_2_out, Instruction[16]);
  not not_3 (not_3_out, Instruction[15]);
  and and_3 (Load_Enable, Instruction[17], not_2_out, not_3_out);
  not not_4 (not_4_out, Instruction[17]);
  or or_1 (Write_Enable, Load_Enable, not_4_out);
  and and_4 (and_4_out, Instruction[15], Instruction[16]);
  Multiplexer #(.width(4), .enable("false")) multiplexer_1 (
    .in0(Instruction[14:11]), .in1(Instruction[11:8]), .out(multiplexer_1_out), .sel(and_4_out));
  Multiplexer #(.width(4), .enable("false")) multiplexer_2 (
    .in0(Instruction[10:7]), .in1(multiplexer_1_out), .out(Read_Address_1), .sel(Instruction[17]));
  Multiplexer #(.width(4), .enable("false")) multiplexer_3 (
    .in0(Instruction[3:0]), .in1(Instruction[7:4]), .out(Read_Address_2), .sel(Instruction[17]));

  assign ALU_Type = Instruction[16:15];
  assign BR_Address = Instruction[3:0];
  assign DM_Address = Instruction[9:0];
  assign Imm_Selector = Instruction[6];
  assign JMP___BR_Selector = Instruction[15];
  assign JMP_Address = Instruction[14:0];
  assign nzp = Instruction[14:12];
  assign Write_Address = Instruction[14:11];
  assign Write_Data_Selector = Instruction[17];

  // Notes on the sheet:
  //   OP2
  //   OP1
  //   SRC2 | ADDR
  //   SRC1
  //   DST | SRC
  //   opcode
  //   ST | BR
endmodule

module ALU (
  input  [17:0] Reg1,
  input  [17:0] Reg2_Or_Imm,
  input  [1:0] Type,
  output [17:0] Result
);

  wire [17:0] and_1_out, n18_bit_adder_1_result, or_1_out, xor_1_out;

  assign and_1_out = Reg1 & Reg2_Or_Imm;  // AND_Gate and_1, 18 bits wide
  assign or_1_out = Reg1 | Reg2_Or_Imm;  // OR_Gate or_1, 18 bits wide
  _18_bit_Adder u_18_bit_adder_1 (.Input_1(Reg1), .Input_2(Reg2_Or_Imm), .Result(n18_bit_adder_1_result));
  assign xor_1_out = Reg1 ^ Reg2_Or_Imm;  // XOR_Gate xor_1, 18 bits wide
  Multiplexer #(.select(2), .width(18), .enable("false")) multiplexer_1 (
    .in0(n18_bit_adder_1_result), .in1(and_1_out), .in2(or_1_out), .in3(xor_1_out), .out(Result), .sel(Type));
endmodule

// DM
module DataMemory (
  input  [9:0] Address,
  input  [17:0] Data,
  input  Store,
  input  Clock,
  input  Load,
  input  Clear,
  output [17:0] Output
);

  RAM #(.addrWidth(10), .dataWidth(18), .bus("separate")) ram_1 (
    .addr(Address), .din(Data), .data(Output), .str(Store), .clk(Clock), .ld(Load), .clr(Clear));  // open: sel
endmodule

// RF
module RegisterFile (
  input  [3:0] Read_Addr_1,
  input  [3:0] Read_Addr_2,
  input  Write_Enable,
  input  [3:0] Write_Addr,
  input  [17:0] Write_Data,
  input  Clock,
  input  Clear,
  output [17:0] Read_Data_1,
  output [17:0] Read_Data_2
);

  wire decoder_1_out0, decoder_1_out1, decoder_1_out2, decoder_1_out3, decoder_1_out4, decoder_1_out5,
       decoder_1_out6, decoder_1_out7, decoder_1_out8, decoder_1_out9, decoder_1_out10, decoder_1_out11,
       decoder_1_out12, decoder_1_out13, decoder_1_out14, decoder_1_out15;
  wire [17:0] R0_q, R1_q, R2_q, R3_q, R4_q, R5_q, R6_q, R7_q, R8_q, R9_q, R10_q, R11_q, R12_q, R13_q, R14_q,
       R15_q;

  Decoder #(.select(4)) decoder_1 (
    .out0(decoder_1_out0), .out1(decoder_1_out1), .out2(decoder_1_out2), .out3(decoder_1_out3),
    .out4(decoder_1_out4), .out5(decoder_1_out5), .out6(decoder_1_out6), .out7(decoder_1_out7),
    .out8(decoder_1_out8), .out9(decoder_1_out9), .out10(decoder_1_out10), .out11(decoder_1_out11),
    .out12(decoder_1_out12), .out13(decoder_1_out13), .out14(decoder_1_out14), .out15(decoder_1_out15),
    .sel(Write_Addr), .en(Write_Enable));
  Register #(.width(18)) R0 (.D(Write_Data), .en(decoder_1_out0), .Q(R0_q), .clk(Clock), .clr(Clear));
  Register #(.width(18)) R1 (.D(Write_Data), .en(decoder_1_out1), .Q(R1_q), .clk(Clock), .clr(Clear));
  Register #(.width(18)) R2 (.D(Write_Data), .en(decoder_1_out2), .Q(R2_q), .clk(Clock), .clr(Clear));
  Register #(.width(18)) R3 (.D(Write_Data), .en(decoder_1_out3), .Q(R3_q), .clk(Clock), .clr(Clear));
  Register #(.width(18)) R4 (.D(Write_Data), .en(decoder_1_out4), .Q(R4_q), .clk(Clock), .clr(Clear));
  Register #(.width(18)) R5 (.D(Write_Data), .en(decoder_1_out5), .Q(R5_q), .clk(Clock), .clr(Clear));
  Register #(.width(18)) R6 (.D(Write_Data), .en(decoder_1_out6), .Q(R6_q), .clk(Clock), .clr(Clear));
  Register #(.width(18)) R7 (.D(Write_Data), .en(decoder_1_out7), .Q(R7_q), .clk(Clock), .clr(Clear));
  Register #(.width(18)) R8 (.D(Write_Data), .en(decoder_1_out8), .Q(R8_q), .clk(Clock), .clr(Clear));
  Register #(.width(18)) R9 (.D(Write_Data), .en(decoder_1_out9), .Q(R9_q), .clk(Clock), .clr(Clear));
  Register #(.width(18)) R10 (.D(Write_Data), .en(decoder_1_out10), .Q(R10_q), .clk(Clock), .clr(Clear));
  Register #(.width(18)) R11 (.D(Write_Data), .en(decoder_1_out11), .Q(R11_q), .clk(Clock), .clr(Clear));
  Register #(.width(18)) R12 (.D(Write_Data), .en(decoder_1_out12), .Q(R12_q), .clk(Clock), .clr(Clear));
  Register #(.width(18)) R13 (.D(Write_Data), .en(decoder_1_out13), .Q(R13_q), .clk(Clock), .clr(Clear));
  Register #(.width(18)) R14 (.D(Write_Data), .en(decoder_1_out14), .Q(R14_q), .clk(Clock), .clr(Clear));
  Register #(.width(18)) R15 (.D(Write_Data), .en(decoder_1_out15), .Q(R15_q), .clk(Clock), .clr(Clear));
  Multiplexer #(.select(4), .width(18), .enable("false")) multiplexer_1 (
    .in0(R0_q), .in1(R1_q), .in2(R2_q), .in3(R3_q), .in4(R4_q), .in5(R5_q), .in6(R6_q), .in7(R7_q),
    .in8(R8_q), .in9(R9_q), .in10(R10_q), .in11(R11_q), .in12(R12_q), .in13(R13_q), .in14(R14_q),
    .in15(R15_q), .out(Read_Data_1), .sel(Read_Addr_1));
  Multiplexer #(.select(4), .width(18), .enable("false")) multiplexer_2 (
    .in0(R0_q), .in1(R1_q), .in2(R2_q), .in3(R3_q), .in4(R4_q), .in5(R5_q), .in6(R6_q), .in7(R7_q),
    .in8(R8_q), .in9(R9_q), .in10(R10_q), .in11(R11_q), .in12(R12_q), .in13(R13_q), .in14(R14_q),
    .in15(R15_q), .out(Read_Data_2), .sel(Read_Addr_2));
endmodule

// IM
module \InstrıctionMemory  (
  input  Clock,
  input  [17:0] JumpAddr,
  input  Reset,
  output [17:0] Instruction
);

  wire and_1_out;
  wire [17:0] multiplexer_1_out, n18_bit_adder_1_result, PC_q;

  Multiplexer #(.width(18), .enable("false")) multiplexer_1 (
    .in0(18'h1), .in1(JumpAddr), .out(multiplexer_1_out), .sel(and_1_out));
  and and_1 (and_1_out, Instruction[16], Instruction[17]);
  Register #(.width(18)) PC (.D(n18_bit_adder_1_result), .Q(PC_q), .clk(Clock), .clr(Reset));  // open: en
  _18_bit_Adder u_18_bit_adder_1 (.Input_1(PC_q), .Input_2(multiplexer_1_out), .Result(n18_bit_adder_1_result));
  ROM #(.addrWidth(18), .dataWidth(18)) rom_1 (.addr(PC_q), .data(Instruction));  // open: sel

  // Notes on the sheet:
  //   contents of rom_1 (hex, n*v repeats v):
  //   46 108d8 1882 905a 28000 29801 1a082 1a947 3e202 8005 8040 884 d084 5502 39a32 37ffe 99c0 23801
endmodule

// JMP
module JumpInstruction (
  input  [14:0] In,
  output [17:0] Out
);

  _15_18_SignExtender u_15_18_signextender_1 (.In(In), .Out(Out));
endmodule

// BR
module BranchInstruction (
  input  [3:0] Address,
  input  [17:0] OP1,
  input  [17:0] OP2,
  input  [2:0] nzp,
  output [17:0] Address_2
);

  wire and_1_out, and_2_out, and_3_out, comparator_1_n, comparator_1_p, comparator_1_z, or_1_out;
  wire [17:0] n4_18_signextender_1_out;

  _4_18_SignExtender u_4_18_signextender_1 (.In(Address), .Out(n4_18_signextender_1_out));
  Comparator comparator_1 (.a(OP1), .b(OP2), .p(comparator_1_p), .z(comparator_1_z), .n(comparator_1_n));
  and and_1 (and_1_out, comparator_1_p, nzp[0]);
  and and_2 (and_2_out, comparator_1_z, nzp[1]);
  and and_3 (and_3_out, comparator_1_n, nzp[2]);
  or or_1 (or_1_out, and_1_out, and_2_out, and_3_out);
  Multiplexer #(.width(18), .enable("false")) multiplexer_1 (
    .in0(18'h1), .in1(n4_18_signextender_1_out), .out(Address_2), .sel(or_1_out));
endmodule

// HA
module HalfAdder (
  input  a,
  input  b,
  output co,
  output s
);

  and and_1 (co, a, b);
  xor xor_1 (s, a, b);
endmodule

// FA
module FullAdder (
  input  a,
  input  b,
  input  ci,
  output co,
  output s
);

  wire and_1_out, and_2_out, and_3_out, xor_1_out;

  and and_1 (and_1_out, a, ci);
  and and_2 (and_2_out, a, b);
  or or_1 (co, and_2_out, and_1_out, and_3_out);
  and and_3 (and_3_out, b, ci);
  xor xor_1 (xor_1_out, a, b);
  xor xor_2 (s, xor_1_out, ci);
endmodule

// Adder
module _18_bit_Adder (
  input  [17:0] Input_1,
  input  [17:0] Input_2,
  output [17:0] Result
);

  wire fulladder_2_co, fulladder_3_co, fulladder_4_co, fulladder_5_co, fulladder_6_co, fulladder_7_co,
       fulladder_8_co, fulladder_9_co, fulladder_10_co, fulladder_11_co, fulladder_12_co, fulladder_13_co,
       fulladder_14_co, fulladder_15_co, fulladder_16_co, fulladder_17_co, halfadder_1_co;

  FullAdder fulladder_1 (.a(Input_1[17]), .b(Input_2[17]), .ci(fulladder_2_co), .s(Result[17]));  // open: co
  FullAdder fulladder_2 (.a(Input_1[16]), .b(Input_2[16]), .ci(fulladder_3_co), .co(fulladder_2_co), .s(Result[16]));
  FullAdder fulladder_3 (.a(Input_1[15]), .b(Input_2[15]), .ci(fulladder_4_co), .co(fulladder_3_co), .s(Result[15]));
  FullAdder fulladder_4 (.a(Input_1[14]), .b(Input_2[14]), .ci(fulladder_5_co), .co(fulladder_4_co), .s(Result[14]));
  FullAdder fulladder_5 (.a(Input_1[13]), .b(Input_2[13]), .ci(fulladder_6_co), .co(fulladder_5_co), .s(Result[13]));
  FullAdder fulladder_6 (.a(Input_1[12]), .b(Input_2[12]), .ci(fulladder_8_co), .co(fulladder_6_co), .s(Result[12]));
  FullAdder fulladder_7 (.a(Input_1[10]), .b(Input_2[10]), .ci(fulladder_9_co), .co(fulladder_7_co), .s(Result[10]));
  FullAdder fulladder_8 (.a(Input_1[11]), .b(Input_2[11]), .ci(fulladder_7_co), .co(fulladder_8_co), .s(Result[11]));
  FullAdder fulladder_9 (.a(Input_1[9]), .b(Input_2[9]), .ci(fulladder_10_co), .co(fulladder_9_co), .s(Result[9]));
  FullAdder fulladder_10 (.a(Input_1[8]), .b(Input_2[8]), .ci(fulladder_11_co), .co(fulladder_10_co), .s(Result[8]));
  FullAdder fulladder_11 (.a(Input_1[7]), .b(Input_2[7]), .ci(fulladder_12_co), .co(fulladder_11_co), .s(Result[7]));
  FullAdder fulladder_12 (.a(Input_1[6]), .b(Input_2[6]), .ci(fulladder_13_co), .co(fulladder_12_co), .s(Result[6]));
  FullAdder fulladder_13 (.a(Input_1[5]), .b(Input_2[5]), .ci(fulladder_14_co), .co(fulladder_13_co), .s(Result[5]));
  FullAdder fulladder_14 (.a(Input_1[4]), .b(Input_2[4]), .ci(fulladder_15_co), .co(fulladder_14_co), .s(Result[4]));
  FullAdder fulladder_15 (.a(Input_1[3]), .b(Input_2[3]), .ci(fulladder_16_co), .co(fulladder_15_co), .s(Result[3]));
  FullAdder fulladder_16 (.a(Input_1[2]), .b(Input_2[2]), .ci(fulladder_17_co), .co(fulladder_16_co), .s(Result[2]));
  FullAdder fulladder_17 (.a(Input_1[1]), .b(Input_2[1]), .ci(halfadder_1_co), .co(fulladder_17_co), .s(Result[1]));
  HalfAdder halfadder_1 (.a(Input_1[0]), .b(Input_2[0]), .co(halfadder_1_co), .s(Result[0]));
endmodule

// CS
module ComparatorStage (
  input  a,
  input  b,
  input  Igt,
  input  Ieq,
  input  Ilt,
  output ogt,
  output oeq,
  output olt
);

  wire and_1_out, and_3_out, not_1_out, not_2_out, xnor_1_out;

  not not_1 (not_1_out, b);
  not not_2 (not_2_out, a);
  xnor xnor_1 (xnor_1_out, b, a);
  and and_1 (and_1_out, not_1_out, a, Ieq);
  or or_1 (ogt, and_1_out, Igt);
  and and_2 (oeq, xnor_1_out, Ieq);
  and and_3 (and_3_out, Ieq, b, not_2_out);
  or or_2 (olt, and_3_out, Ilt);
endmodule

// CMP
module Comparator (
  input  [17:0] a,
  input  [17:0] b,
  output p,
  output z,
  output n
);

  wire and_1_out, and_2_out, comparatorstage_1_oeq, comparatorstage_1_ogt, comparatorstage_1_olt,
       comparatorstage_2_oeq, comparatorstage_2_ogt, comparatorstage_2_olt, comparatorstage_3_oeq,
       comparatorstage_3_ogt, comparatorstage_3_olt, comparatorstage_4_oeq, comparatorstage_4_ogt,
       comparatorstage_4_olt, comparatorstage_5_oeq, comparatorstage_5_ogt, comparatorstage_5_olt,
       comparatorstage_6_oeq, comparatorstage_6_ogt, comparatorstage_6_olt, comparatorstage_7_oeq,
       comparatorstage_7_ogt, comparatorstage_7_olt, comparatorstage_8_oeq, comparatorstage_8_ogt,
       comparatorstage_8_olt, comparatorstage_9_oeq, comparatorstage_9_ogt, comparatorstage_9_olt,
       comparatorstage_10_oeq, comparatorstage_10_ogt, comparatorstage_10_olt, comparatorstage_11_oeq,
       comparatorstage_11_ogt, comparatorstage_11_olt, comparatorstage_12_oeq, comparatorstage_12_ogt,
       comparatorstage_12_olt, comparatorstage_13_oeq, comparatorstage_13_ogt, comparatorstage_13_olt,
       comparatorstage_14_oeq, comparatorstage_14_ogt, comparatorstage_14_olt, comparatorstage_15_oeq,
       comparatorstage_15_ogt, comparatorstage_15_olt, comparatorstage_16_oeq, comparatorstage_16_ogt,
       comparatorstage_16_olt, comparatorstage_17_ogt, comparatorstage_17_olt, not_1_out, not_2_out,
       not_3_out, xor_1_out;

  not not_1 (not_1_out, xor_1_out);
  ComparatorStage comparatorstage_1 (
    .Igt(1'b0), .Ieq(not_1_out), .Ilt(1'b0), .a(a[16]), .b(b[16]), .ogt(comparatorstage_1_ogt),
    .oeq(comparatorstage_1_oeq), .olt(comparatorstage_1_olt));
  ComparatorStage comparatorstage_2 (
    .Igt(comparatorstage_1_ogt), .Ieq(comparatorstage_1_oeq), .Ilt(comparatorstage_1_olt), .a(a[15]),
    .b(b[15]), .ogt(comparatorstage_2_ogt), .oeq(comparatorstage_2_oeq), .olt(comparatorstage_2_olt));
  ComparatorStage comparatorstage_3 (
    .Igt(comparatorstage_2_ogt), .Ieq(comparatorstage_2_oeq), .Ilt(comparatorstage_2_olt), .a(a[14]),
    .b(b[14]), .ogt(comparatorstage_3_ogt), .oeq(comparatorstage_3_oeq), .olt(comparatorstage_3_olt));
  ComparatorStage comparatorstage_4 (
    .Igt(comparatorstage_3_ogt), .Ieq(comparatorstage_3_oeq), .Ilt(comparatorstage_3_olt), .a(a[13]),
    .b(b[13]), .ogt(comparatorstage_4_ogt), .oeq(comparatorstage_4_oeq), .olt(comparatorstage_4_olt));
  ComparatorStage comparatorstage_5 (
    .Igt(comparatorstage_4_ogt), .Ieq(comparatorstage_4_oeq), .Ilt(comparatorstage_4_olt), .a(a[12]),
    .b(b[12]), .ogt(comparatorstage_5_ogt), .oeq(comparatorstage_5_oeq), .olt(comparatorstage_5_olt));
  not not_2 (not_2_out, b[17]);
  not not_3 (not_3_out, a[17]);
  ComparatorStage comparatorstage_6 (
    .Igt(comparatorstage_5_ogt), .Ieq(comparatorstage_5_oeq), .Ilt(comparatorstage_5_olt), .a(a[11]),
    .b(b[11]), .ogt(comparatorstage_6_ogt), .oeq(comparatorstage_6_oeq), .olt(comparatorstage_6_olt));
  and and_1 (and_1_out, not_2_out, a[17]);
  and and_2 (and_2_out, not_3_out, b[17]);
  xor xor_1 (xor_1_out, a[17], b[17]);
  ComparatorStage comparatorstage_7 (
    .Igt(comparatorstage_6_ogt), .Ieq(comparatorstage_6_oeq), .Ilt(comparatorstage_6_olt), .a(a[10]),
    .b(b[10]), .ogt(comparatorstage_7_ogt), .oeq(comparatorstage_7_oeq), .olt(comparatorstage_7_olt));
  ComparatorStage comparatorstage_8 (
    .Igt(comparatorstage_7_ogt), .Ieq(comparatorstage_7_oeq), .Ilt(comparatorstage_7_olt), .a(a[9]),
    .b(b[9]), .ogt(comparatorstage_8_ogt), .oeq(comparatorstage_8_oeq), .olt(comparatorstage_8_olt));
  ComparatorStage comparatorstage_9 (
    .Igt(comparatorstage_8_ogt), .Ieq(comparatorstage_8_oeq), .Ilt(comparatorstage_8_olt), .a(a[8]),
    .b(b[8]), .ogt(comparatorstage_9_ogt), .oeq(comparatorstage_9_oeq), .olt(comparatorstage_9_olt));
  ComparatorStage comparatorstage_10 (
    .Igt(comparatorstage_9_ogt), .Ieq(comparatorstage_9_oeq), .Ilt(comparatorstage_9_olt), .a(a[7]),
    .b(b[7]), .ogt(comparatorstage_10_ogt), .oeq(comparatorstage_10_oeq), .olt(comparatorstage_10_olt));
  Multiplexer #(.enable("false")) multiplexer_1 (
    .in0(comparatorstage_17_ogt), .in1(and_2_out), .out(p), .sel(xor_1_out));
  ComparatorStage comparatorstage_11 (
    .Igt(comparatorstage_12_ogt), .Ieq(comparatorstage_12_oeq), .Ilt(comparatorstage_12_olt), .a(a[5]),
    .b(b[5]), .ogt(comparatorstage_11_ogt), .oeq(comparatorstage_11_oeq), .olt(comparatorstage_11_olt));
  ComparatorStage comparatorstage_12 (
    .Igt(comparatorstage_10_ogt), .Ieq(comparatorstage_10_oeq), .Ilt(comparatorstage_10_olt), .a(a[6]),
    .b(b[6]), .ogt(comparatorstage_12_ogt), .oeq(comparatorstage_12_oeq), .olt(comparatorstage_12_olt));
  Multiplexer #(.enable("false")) multiplexer_2 (
    .in0(comparatorstage_17_olt), .in1(and_1_out), .out(n), .sel(xor_1_out));
  ComparatorStage comparatorstage_13 (
    .Igt(comparatorstage_11_ogt), .Ieq(comparatorstage_11_oeq), .Ilt(comparatorstage_11_olt), .a(a[4]),
    .b(b[4]), .ogt(comparatorstage_13_ogt), .oeq(comparatorstage_13_oeq), .olt(comparatorstage_13_olt));
  ComparatorStage comparatorstage_14 (
    .Igt(comparatorstage_13_ogt), .Ieq(comparatorstage_13_oeq), .Ilt(comparatorstage_13_olt), .a(a[3]),
    .b(b[3]), .ogt(comparatorstage_14_ogt), .oeq(comparatorstage_14_oeq), .olt(comparatorstage_14_olt));
  ComparatorStage comparatorstage_15 (
    .Igt(comparatorstage_14_ogt), .Ieq(comparatorstage_14_oeq), .Ilt(comparatorstage_14_olt), .a(a[2]),
    .b(b[2]), .ogt(comparatorstage_15_ogt), .oeq(comparatorstage_15_oeq), .olt(comparatorstage_15_olt));
  ComparatorStage comparatorstage_16 (
    .Igt(comparatorstage_15_ogt), .Ieq(comparatorstage_15_oeq), .Ilt(comparatorstage_15_olt), .a(a[1]),
    .b(b[1]), .ogt(comparatorstage_16_ogt), .oeq(comparatorstage_16_oeq), .olt(comparatorstage_16_olt));
  ComparatorStage comparatorstage_17 (
    .Igt(comparatorstage_16_ogt), .Ieq(comparatorstage_16_oeq), .Ilt(comparatorstage_16_olt), .a(a[0]),
    .b(b[0]), .ogt(comparatorstage_17_ogt), .oeq(z), .olt(comparatorstage_17_olt));
endmodule

// SE
module _4_18_SignExtender (
  input  [3:0] In,
  output [17:0] Out
);


  assign Out = {{15{In[3]}}, In[2:0]};
endmodule

// SE
module _6_18_SignExtender (
  input  [5:0] In,
  output [17:0] Out
);


  assign Out = {{13{In[5]}}, In[4:0]};
endmodule

// SE
module _15_18_SignExtender (
  input  [14:0] In,
  output [17:0] Out
);


  assign Out = {{4{In[14]}}, In[13:0]};
endmodule
